// Logisim project lite16.circ as structural Verilog: 4 circuits, main circuit main
module main (
);

  wire and_1_out, and_2_out, and_4_out, and_5_out, and_6_out, and_7_out, and_8_out, and_9_out, and_10_out,
       and_11_out, bitselector_1_out, bitselector_6_out, bitselector_7_out, bitselector_8_out, clock_1_out,
       CMP_out, comparator_1_eq, comparator_1_gt, comparator_1_lt, demultiplexer_1_out0,
       demultiplexer_1_out1, demultiplexer_1_out2, demultiplexer_1_out3, demultiplexer_1_out4,
       demultiplexer_1_out5, demultiplexer_1_out6, demultiplexer_1_out7, demultiplexer_1_out8,
       demultiplexer_1_out9, demultiplexer_1_out10, demultiplexer_1_out11, demultiplexer_1_out12,
       demultiplexer_1_out13, demultiplexer_1_out14, demultiplexer_1_out15, FN_out, JMP_out, LD_out, MEM_out,
       multiplexer_9_out, not_1_out, not_2_out, not_3_out, not_4_out, not_5_out, not_6_out, not_7_out,
       not_8_out, or_1_out, R_prime_I_out, ST_out;
  wire [1:0] bitselector_10_out;
  wire [3:0] bitselector_2_out, bitselector_3_out, bitselector_4_out, bitselector_5_out, bitselector_9_out,
       multiplexer_2_out;
  wire [15:0] _0_q, _1_q, _2_q, _3_q, _4_q, _5_q, _6_q, _7_q, _8_q, _9_q, _10_q, _11_q, _12_q, _13_q, _14_q,
       _15_q, adder_1_out, adder_2_out, adder_3_out, adder_4_out, and_3_out, and_12_out, and_13_out,
       and_14_out, and_15_out, and_16_out, and_17_out, and_18_out, and_19_out, bit_extender_1_out,
       bit_extender_2_out, bit_extender_3_out, bit_extender_4_out, bit_extender_5_out, bit_extender_6_out,
       bit_extender_7_out, bit_extender_8_out, bit_extender_9_out, bit_extender_10_out, multiplexer_1_out,
       multiplexer_3_out, multiplexer_4_out, multiplexer_5_out, multiplexer_6_out, multiplexer_7_out,
       multiplexer_8_out, multiplexer_10_out, multiplexer_11_out, multiplexer_12_out, or_2_out, or_3_out,
       or_4_out, or_5_out, or_6_out, or_7_out, or_8_out, or_9_out, PC_q, ram_1_data, rom_1_data,
       shifter_1_out, shifter_2_out, shifter_3_out, shifter_4_out, shifter_5_out, xor_1_out;

  Clock clock_1 (.out(clock_1_out));
  Register #(.width(16)) PC (.D(multiplexer_1_out), .Q(PC_q), .clk(clock_1_out));  // open: en, clr
  Multiplexer #(.width(16), .enable("false")) multiplexer_1 (
    .in0(adder_2_out), .in1(adder_1_out), .out(multiplexer_1_out), .sel(and_1_out));
  Adder #(.width(16)) adder_1 (.a(PC_q), .b(multiplexer_6_out), .out(adder_1_out));  // open: cin, cout
  and R_prime_I (R_prime_I_out, bitselector_1_out, bitselector_6_out, bitselector_7_out);
  Adder #(.width(16)) adder_2 (.a(PC_q), .b(16'h1), .out(adder_2_out));  // open: cin, cout
  and and_1 (and_1_out, multiplexer_9_out, JMP_out);
  BitSelector #(.width(4)) bitselector_1 (.in(bitselector_2_out), .out(bitselector_1_out), .sel(2'b11));
  and CMP (CMP_out, bitselector_7_out, bitselector_8_out);
  BitSelector #(.width(16), .group(4)) bitselector_2 (.in(rom_1_data), .out(bitselector_2_out), .sel(2'b00));
  BitSelector #(.width(16), .group(4)) bitselector_3 (.in(rom_1_data), .out(bitselector_3_out), .sel(2'b01));
  BitSelector #(.width(16), .group(4)) bitselector_4 (.in(rom_1_data), .out(bitselector_4_out), .sel(2'b10));
  BitSelector #(.width(16), .group(4)) bitselector_5 (.in(rom_1_data), .out(bitselector_5_out), .sel(2'b11));
  BitSelector #(.width(4)) bitselector_6 (.in(bitselector_2_out), .out(bitselector_6_out), .sel(2'b10));
  not not_1 (not_1_out, bitselector_6_out);
  BitSelector #(.width(4)) bitselector_7 (.in(bitselector_2_out), .out(bitselector_7_out), .sel(2'b01));
  not not_2 (not_2_out, bitselector_7_out);
  and MEM (MEM_out, bitselector_1_out, bitselector_6_out, not_2_out);
  not not_3 (not_3_out, bitselector_8_out);
  and LD (LD_out, MEM_out, not_3_out);
  ROM #(.addrWidth(16), .dataWidth(16)) rom_1 (.addr(PC_q), .data(rom_1_data));  // open: sel
  BitSelector #(.width(4)) bitselector_8 (.in(bitselector_2_out), .out(bitselector_8_out), .sel(2'b00));
  and JMP (JMP_out, bitselector_1_out, not_1_out);
  and ST (ST_out, MEM_out, bitselector_8_out);
  and FN (FN_out, JMP_out, CMP_out);
  not not_4 (not_4_out, FN_out);
  and and_2 (and_2_out, not_4_out, JMP_out);
  not not_5 (not_5_out, or_1_out);
  or or_1 (or_1_out, and_2_out, ST_out);
  Demultiplexer #(.select(4), .enable("false")) demultiplexer_1 (
    .out0(demultiplexer_1_out0), .out1(demultiplexer_1_out1), .out2(demultiplexer_1_out2),
    .out3(demultiplexer_1_out3), .out4(demultiplexer_1_out4), .out5(demultiplexer_1_out5),
    .out6(demultiplexer_1_out6), .out7(demultiplexer_1_out7), .out8(demultiplexer_1_out8),
    .out9(demultiplexer_1_out9), .out10(demultiplexer_1_out10), .out11(demultiplexer_1_out11),
    .out12(demultiplexer_1_out12), .out13(demultiplexer_1_out13), .out14(demultiplexer_1_out14),
    .out15(demultiplexer_1_out15), .in(not_5_out), .sel(multiplexer_2_out));
  Multiplexer #(.width(4), .enable("false")) multiplexer_2 (
    .in0(bitselector_5_out), .in1(bitselector_4_out), .out(multiplexer_2_out), .sel(FN_out));
  Multiplexer #(.width(16), .enable("false")) multiplexer_3 (
    .in0(multiplexer_12_out), .in1(adder_2_out), .out(multiplexer_3_out), .sel(JMP_out));
  Register #(.width(16)) _0 (
    .D(multiplexer_3_out), .en(demultiplexer_1_out0), .Q(_0_q), .clk(clock_1_out));  // open: clr
  Register #(.width(16)) _1 (
    .D(multiplexer_3_out), .en(demultiplexer_1_out1), .Q(_1_q), .clk(clock_1_out));  // open: clr
  Register #(.width(16)) _2 (
    .D(multiplexer_3_out), .en(demultiplexer_1_out2), .Q(_2_q), .clk(clock_1_out));  // open: clr
  Register #(.width(16)) _3 (
    .D(multiplexer_3_out), .en(demultiplexer_1_out3), .Q(_3_q), .clk(clock_1_out));  // open: clr
  Register #(.width(16)) _4 (
    .D(multiplexer_3_out), .en(demultiplexer_1_out4), .Q(_4_q), .clk(clock_1_out));  // open: clr
  Register #(.width(16)) _5 (
    .D(multiplexer_3_out), .en(demultiplexer_1_out5), .Q(_5_q), .clk(clock_1_out));  // open: clr
  Register #(.width(16)) _6 (
    .D(multiplexer_3_out), .en(demultiplexer_1_out6), .Q(_6_q), .clk(clock_1_out));  // open: clr
  Register #(.width(16)) _7 (
    .D(multiplexer_3_out), .en(demultiplexer_1_out7), .Q(_7_q), .clk(clock_1_out));  // open: clr
  Register #(.width(16)) _8 (
    .D(multiplexer_3_out), .en(demultiplexer_1_out8), .Q(_8_q), .clk(clock_1_out));  // open: clr
  Register #(.width(16)) _9 (
    .D(multiplexer_3_out), .en(demultiplexer_1_out9), .Q(_9_q), .clk(clock_1_out));  // open: clr
  Register #(.width(16)) _10 (
    .D(multiplexer_3_out), .en(demultiplexer_1_out10), .Q(_10_q), .clk(clock_1_out));  // open: clr
  Register #(.width(16)) _11 (
    .D(multiplexer_3_out), .en(demultiplexer_1_out11), .Q(_11_q), .clk(clock_1_out));  // open: clr
  Register #(.width(16)) _12 (
    .D(multiplexer_3_out), .en(demultiplexer_1_out12), .Q(_12_q), .clk(clock_1_out));  // open: clr
  Register #(.width(16)) _13 (
    .D(multiplexer_3_out), .en(demultiplexer_1_out13), .Q(_13_q), .clk(clock_1_out));  // open: clr
  Register #(.width(16)) _14 (
    .D(multiplexer_3_out), .en(demultiplexer_1_out14), .Q(_14_q), .clk(clock_1_out));  // open: clr
  Register #(.width(16)) _15 (
    .D(multiplexer_3_out), .en(demultiplexer_1_out15), .Q(_15_q), .clk(clock_1_out));  // open: clr
  Multiplexer #(.select(4), .width(16), .enable("false")) multiplexer_4 (
    .in0(_0_q), .in1(_1_q), .in2(_2_q), .in3(_3_q), .in4(_4_q), .in5(_5_q), .in6(_6_q), .in7(_7_q),
    .in8(_8_q), .in9(_9_q), .in10(_10_q), .in11(_11_q), .in12(_12_q), .in13(_13_q), .in14(_14_q),
    .in15(_15_q), .out(multiplexer_4_out), .sel(bitselector_3_out));
  Multiplexer #(.select(4), .width(16), .enable("false")) multiplexer_5 (
    .in0(_0_q), .in1(_1_q), .in2(_2_q), .in3(_3_q), .in4(_4_q), .in5(_5_q), .in6(_6_q), .in7(_7_q),
    .in8(_8_q), .in9(_9_q), .in10(_10_q), .in11(_11_q), .in12(_12_q), .in13(_13_q), .in14(_14_q),
    .in15(_15_q), .out(multiplexer_5_out), .sel(bitselector_4_out));
  Multiplexer #(.select(4), .width(16), .enable("false")) multiplexer_6 (
    .in0(_0_q), .in1(_1_q), .in2(_2_q), .in3(_3_q), .in4(_4_q), .in5(_5_q), .in6(_6_q), .in7(_7_q),
    .in8(_8_q), .in9(_9_q), .in10(_10_q), .in11(_11_q), .in12(_12_q), .in13(_13_q), .in14(_14_q),
    .in15(_15_q), .out(multiplexer_6_out), .sel(bitselector_5_out));
  assign bit_extender_1_out = {{12{1'b0}}, bitselector_3_out};  // Bit_Extender bit_extender_1
  assign bit_extender_2_out = {{12{1'b0}}, bitselector_4_out};  // Bit_Extender bit_extender_2
  Shifter #(.width(16)) shifter_1 (.in(bit_extender_2_out), .\dist (4'b0100), .out(shifter_1_out));
  Multiplexer #(.width(16), .enable("false")) multiplexer_7 (
    .in0(multiplexer_4_out), .in1(bit_extender_1_out), .out(multiplexer_7_out), .sel(R_prime_I_out));
  Multiplexer #(.width(16), .enable("false")) multiplexer_8 (
    .in0(multiplexer_5_out), .in1(shifter_1_out), .out(multiplexer_8_out), .sel(R_prime_I_out));
  BitSelector #(.width(16), .group(4)) bitselector_9 (.in(multiplexer_8_out), .out(bitselector_9_out), .sel(2'b00));
  Adder #(.width(16)) adder_3 (.a(multiplexer_7_out), .b(multiplexer_8_out), .out(adder_3_out));  // open: cin, cout
  assign or_2_out = multiplexer_7_out | multiplexer_8_out;  // OR_Gate or_2, 16 bits wide
  assign xor_1_out = multiplexer_7_out ^ multiplexer_8_out;  // XOR_Gate xor_1, 16 bits wide
  assign and_3_out = multiplexer_7_out & multiplexer_8_out;  // AND_Gate and_3, 16 bits wide
  Shifter #(.width(16)) shifter_2 (.in(multiplexer_7_out), .\dist (bitselector_9_out), .out(shifter_2_out));
  Shifter #(.width(16), .shift("lr")) shifter_3 (
    .in(multiplexer_7_out), .\dist (bitselector_9_out), .out(shifter_3_out));
  Shifter #(.width(16), .shift("ar")) shifter_4 (
    .in(multiplexer_7_out), .\dist (bitselector_9_out), .out(shifter_4_out));
  RAM #(.addrWidth(16), .dataWidth(16), .bus("separate")) ram_1 (
    .addr(multiplexer_5_out), .din(multiplexer_6_out), .data(ram_1_data), .str(ST_out), .clk(clock_1_out),
    .ld(LD_out));  // open: sel, clr
  not not_6 (not_6_out, bitselector_6_out);
  not not_7 (not_7_out, bitselector_7_out);
  Comparator #(.width(16)) comparator_1 (
    .a(multiplexer_7_out), .b(multiplexer_8_out), .gt(comparator_1_gt), .eq(comparator_1_eq),
    .lt(comparator_1_lt));
  BitSelector #(.width(4), .group(2)) bitselector_10 (.in(bitselector_2_out), .out(bitselector_10_out), .sel(1'b0));
  not not_8 (not_8_out, bitselector_8_out);
  and and_4 (and_4_out, not_8_out, not_7_out, not_6_out);
  and and_5 (and_5_out, bitselector_8_out, not_7_out, not_6_out);
  and and_6 (and_6_out, not_8_out, bitselector_7_out, not_6_out);
  and and_7 (and_7_out, bitselector_8_out, bitselector_7_out, not_6_out);
  and and_8 (and_8_out, not_8_out, not_7_out, bitselector_6_out);
  and and_9 (and_9_out, bitselector_8_out, not_7_out, bitselector_6_out);
  and and_10 (and_10_out, not_8_out, bitselector_7_out, bitselector_6_out);
  and and_11 (and_11_out, bitselector_8_out, bitselector_7_out, bitselector_6_out);
  Multiplexer #(.select(2), .enable("false")) multiplexer_9 (
    .in0(comparator_1_eq), .in1(comparator_1_lt), .in2(comparator_1_gt), .in3(1'b1), .out(multiplexer_9_out),
    .sel(bitselector_10_out));
  assign bit_extender_3_out = {{15{and_4_out}}, and_4_out};  // Bit_Extender bit_extender_3
  assign bit_extender_4_out = {{15{and_5_out}}, and_5_out};  // Bit_Extender bit_extender_4
  assign bit_extender_5_out = {{15{and_6_out}}, and_6_out};  // Bit_Extender bit_extender_5
  assign bit_extender_6_out = {{15{and_7_out}}, and_7_out};  // Bit_Extender bit_extender_6
  assign bit_extender_7_out = {{15{and_8_out}}, and_8_out};  // Bit_Extender bit_extender_7
  assign bit_extender_8_out = {{15{and_9_out}}, and_9_out};  // Bit_Extender bit_extender_8
  assign bit_extender_9_out = {{15{and_10_out}}, and_10_out};  // Bit_Extender bit_extender_9
  assign bit_extender_10_out = {{15{and_11_out}}, and_11_out};  // Bit_Extender bit_extender_10
  assign and_12_out = bit_extender_3_out & adder_3_out;  // AND_Gate and_12, 16 bits wide
  assign or_3_out = and_12_out | and_13_out;  // OR_Gate or_3, 16 bits wide
  assign and_13_out = bit_extender_4_out & or_2_out;  // AND_Gate and_13, 16 bits wide
  assign and_14_out = bit_extender_5_out & xor_1_out;  // AND_Gate and_14, 16 bits wide
  assign or_4_out = and_14_out | and_15_out;  // OR_Gate or_4, 16 bits wide
  assign and_15_out = bit_extender_6_out & and_3_out;  // AND_Gate and_15, 16 bits wide
  assign and_16_out = bit_extender_7_out & shifter_2_out;  // AND_Gate and_16, 16 bits wide
  assign or_5_out = and_16_out | and_17_out;  // OR_Gate or_5, 16 bits wide
  assign and_17_out = bit_extender_8_out & shifter_3_out;  // AND_Gate and_17, 16 bits wide
  assign and_18_out = bit_extender_9_out & shifter_4_out;  // AND_Gate and_18, 16 bits wide
  assign or_6_out = and_18_out | and_19_out;  // OR_Gate or_6, 16 bits wide
  assign and_19_out = bit_extender_10_out & adder_3_out;  // AND_Gate and_19, 16 bits wide
  Adder #(.width(16)) adder_4 (.a(adder_3_out), .b(multiplexer_6_out), .out(adder_4_out));  // open: cin, cout
  Shifter #(.width(16)) shifter_5 (.in(adder_3_out), .\dist (4'b1000), .out(shifter_5_out));
  assign or_7_out = or_3_out | or_4_out;  // OR_Gate or_7, 16 bits wide
  assign or_8_out = or_5_out | or_6_out;  // OR_Gate or_8, 16 bits wide
  Multiplexer #(.width(16), .enable("false")) multiplexer_10 (
    .in0(adder_4_out), .in1(shifter_5_out), .out(multiplexer_10_out), .sel(bitselector_8_out));
  assign or_9_out = or_7_out | or_8_out;  // OR_Gate or_9, 16 bits wide
  Multiplexer #(.width(16), .enable("false")) multiplexer_11 (
    .in0(or_9_out), .in1(multiplexer_10_out), .out(multiplexer_11_out), .sel(R_prime_I_out));
  Multiplexer #(.width(16), .enable("false")) multiplexer_12 (
    .in0(multiplexer_11_out), .in1(ram_1_data), .out(multiplexer_12_out), .sel(LD_out));

  // Notes on the sheet:
  //   (0-3)
  //   (4-7)
  //   (8-11)
  //   (12-15)
  //   contents of rom_1 (hex, n*v repeats v):
  //   101e 207e 210d 310c 401f 5fff 5fee 6450 7121 8122 9123 a114 b1a5 c156 a008 0 a219 0 a21a 7f0b 6*0
  //   120
  //   A
  //   B
endmodule

module ALU (
  input  [2:0] in_1,
  input  [15:0] A,
  input  [15:0] B,
  input  [15:0] rd,
  input  [3:0] _0_3,
  output [15:0] R,
  output [15:0] CMP,
  output CMP_2
);

  wire and_2_out, and_3_out, and_4_out, and_5_out, and_6_out, and_7_out, and_8_out, and_9_out,
       bitselector_2_out, bitselector_3_out, bitselector_4_out, comparator_1_eq, comparator_1_gt,
       comparator_1_lt, not_1_out, not_2_out, not_3_out;
  wire [1:0] bitselector_5_out;
  wire [3:0] bitselector_1_out;
  wire [15:0] adder_1_out, adder_2_out, and_1_out, and_10_out, and_11_out, and_12_out, and_13_out,
       and_14_out, and_15_out, and_16_out, and_17_out, bit_extender_1_out, bit_extender_2_out,
       bit_extender_3_out, bit_extender_4_out, bit_extender_5_out, bit_extender_6_out, bit_extender_7_out,
       bit_extender_8_out, or_1_out, or_2_out, or_3_out, or_4_out, or_5_out, or_6_out, or_7_out,
       shifter_1_out, shifter_2_out, shifter_3_out, shifter_4_out, xor_1_out;

  BitSelector #(.width(16), .group(4)) bitselector_1 (.in(B), .out(bitselector_1_out), .sel(2'b00));
  Adder #(.width(16)) adder_1 (.a(A), .b(B), .out(adder_1_out));  // open: cin, cout
  assign or_1_out = A | B;  // OR_Gate or_1, 16 bits wide
  assign xor_1_out = A ^ B;  // XOR_Gate xor_1, 16 bits wide
  assign and_1_out = A & B;  // AND_Gate and_1, 16 bits wide
  Shifter #(.width(16)) shifter_1 (.in(A), .\dist (bitselector_1_out), .out(shifter_1_out));
  Shifter #(.width(16), .shift("lr")) shifter_2 (.in(A), .\dist (bitselector_1_out), .out(shifter_2_out));
  Shifter #(.width(16), .shift("ar")) shifter_3 (.in(A), .\dist (bitselector_1_out), .out(shifter_3_out));
  BitSelector #(.width(3)) bitselector_2 (.in(in_1), .out(bitselector_2_out), .sel(2'b10));
  not not_1 (not_1_out, bitselector_2_out);
  BitSelector #(.width(3)) bitselector_3 (.in(in_1), .out(bitselector_3_out), .sel(2'b01));
  not not_2 (not_2_out, bitselector_3_out);
  Comparator #(.width(16)) comparator_1 (
    .a(A), .b(B), .gt(comparator_1_gt), .eq(comparator_1_eq), .lt(comparator_1_lt));
  BitSelector #(.width(3)) bitselector_4 (.in(in_1), .out(bitselector_4_out), .sel(2'b00));
  not not_3 (not_3_out, bitselector_4_out);
  Multiplexer #(.select(2), .enable("false")) multiplexer_1 (
    .in0(comparator_1_eq), .in1(comparator_1_lt), .in2(comparator_1_gt), .in3(1'b1), .out(CMP_2),
    .sel(bitselector_5_out));
  BitSelector #(.width(4), .group(2)) bitselector_5 (.in(_0_3), .out(bitselector_5_out), .sel(1'b0));
  assign bit_extender_1_out = {{15{and_2_out}}, and_2_out};  // Bit_Extender bit_extender_1
  and and_2 (and_2_out, not_3_out, not_2_out, not_1_out);
  and and_3 (and_3_out, bitselector_4_out, not_2_out, not_1_out);
  assign bit_extender_2_out = {{15{and_3_out}}, and_3_out};  // Bit_Extender bit_extender_2
  and and_4 (and_4_out, not_3_out, bitselector_3_out, not_1_out);
  assign bit_extender_3_out = {{15{and_4_out}}, and_4_out};  // Bit_Extender bit_extender_3
  and and_5 (and_5_out, bitselector_4_out, bitselector_3_out, not_1_out);
  assign bit_extender_4_out = {{15{and_5_out}}, and_5_out};  // Bit_Extender bit_extender_4
  and and_6 (and_6_out, not_3_out, not_2_out, bitselector_2_out);
  assign bit_extender_5_out = {{15{and_6_out}}, and_6_out};  // Bit_Extender bit_extender_5
  and and_7 (and_7_out, bitselector_4_out, not_2_out, bitselector_2_out);
  assign bit_extender_6_out = {{15{and_7_out}}, and_7_out};  // Bit_Extender bit_extender_6
  and and_8 (and_8_out, not_3_out, bitselector_3_out, bitselector_2_out);
  assign bit_extender_7_out = {{15{and_8_out}}, and_8_out};  // Bit_Extender bit_extender_7
  and and_9 (and_9_out, bitselector_4_out, bitselector_3_out, bitselector_2_out);
  assign bit_extender_8_out = {{15{and_9_out}}, and_9_out};  // Bit_Extender bit_extender_8
  assign and_10_out = bit_extender_1_out & adder_1_out;  // AND_Gate and_10, 16 bits wide
  assign and_11_out = bit_extender_2_out & or_1_out;  // AND_Gate and_11, 16 bits wide
  assign and_12_out = bit_extender_3_out & xor_1_out;  // AND_Gate and_12, 16 bits wide
  assign and_13_out = bit_extender_4_out & and_1_out;  // AND_Gate and_13, 16 bits wide
  assign and_14_out = bit_extender_5_out & shifter_1_out;  // AND_Gate and_14, 16 bits wide
  assign and_15_out = bit_extender_6_out & shifter_2_out;  // AND_Gate and_15, 16 bits wide
  assign and_16_out = bit_extender_7_out & shifter_3_out;  // AND_Gate and_16, 16 bits wide
  assign and_17_out = bit_extender_8_out & adder_1_out;  // AND_Gate and_17, 16 bits wide
  assign or_2_out = and_10_out | and_11_out;  // OR_Gate or_2, 16 bits wide
  assign or_3_out = or_2_out | or_4_out;  // OR_Gate or_3, 16 bits wide
  assign or_4_out = and_12_out | and_13_out;  // OR_Gate or_4, 16 bits wide
  assign or_5_out = and_14_out | and_15_out;  // OR_Gate or_5, 16 bits wide
  assign or_6_out = or_5_out | or_7_out;  // OR_Gate or_6, 16 bits wide
  assign or_7_out = and_16_out | and_17_out;  // OR_Gate or_7, 16 bits wide
  Adder #(.width(16)) adder_2 (.a(adder_1_out), .b(rd), .out(adder_2_out));  // open: cin, cout
  Multiplexer #(.width(16), .enable("false")) multiplexer_2 (
    .in0(adder_2_out), .in1(shifter_4_out), .out(CMP), .sel(bitselector_4_out));
  Shifter #(.width(16)) shifter_4 (.in(adder_1_out), .\dist (4'b1000), .out(shifter_4_out));
  assign R = or_3_out | or_6_out;  // OR_Gate or_8, 16 bits wide
endmodule

module RFU (
  input  [3:0] _0_3,
  input  [3:0] _4_7,
  input  [3:0] _8_11,
  input  [3:0] _12_15,
  input  [15:0] in_5,
  output [15:0] A,
  output [15:0] B
);

  wire and_1_out, bitselector_1_out, bitselector_2_out, bitselector_3_out, bitselector_4_out, clock_1_out,
       CMP_out, demultiplexer_1_out0, demultiplexer_1_out1, demultiplexer_1_out2, demultiplexer_1_out3,
       demultiplexer_1_out4, demultiplexer_1_out5, demultiplexer_1_out6, demultiplexer_1_out7,
       demultiplexer_1_out8, demultiplexer_1_out9, demultiplexer_1_out10, demultiplexer_1_out11,
       demultiplexer_1_out12, demultiplexer_1_out13, demultiplexer_1_out14, demultiplexer_1_out15, FN_out,
       JMP_out, LD_out, MEM_out, not_1_out, not_2_out, not_3_out, not_4_out, not_5_out, or_1_out,
       R_prime_I_out, ST_out;
  wire [3:0] multiplexer_1_out;
  wire [15:0] _0_q, _1_q, _2_q, _3_q, _4_q, _5_q, _6_q, _7_q, _8_q, _9_q, _10_q, _11_q, _12_q, _13_q, _14_q,
       _15_q, bit_extender_1_out, bit_extender_2_out, multiplexer_2_out, multiplexer_3_out;

  and R_prime_I (R_prime_I_out, bitselector_1_out, bitselector_2_out, bitselector_3_out);
  BitSelector #(.width(4)) bitselector_1 (.in(_0_3), .out(bitselector_1_out), .sel(2'b11));
  BitSelector #(.width(4)) bitselector_2 (.in(_0_3), .out(bitselector_2_out), .sel(2'b10));
  not not_1 (not_1_out, bitselector_2_out);
  and CMP (CMP_out, bitselector_3_out, bitselector_4_out);
  BitSelector #(.width(4)) bitselector_3 (.in(_0_3), .out(bitselector_3_out), .sel(2'b01));
  not not_2 (not_2_out, bitselector_3_out);
  and MEM (MEM_out, bitselector_1_out, bitselector_2_out, not_2_out);
  not not_3 (not_3_out, bitselector_4_out);
  and LD (LD_out, MEM_out, not_3_out);
  BitSelector #(.width(4)) bitselector_4 (.in(_0_3), .out(bitselector_4_out), .sel(2'b00));
  and JMP (JMP_out, bitselector_1_out, not_1_out);
  and ST (ST_out, MEM_out, bitselector_4_out);
  and FN (FN_out, JMP_out, CMP_out);
  not not_4 (not_4_out, FN_out);
  and and_1 (and_1_out, not_4_out, JMP_out);
  not not_5 (not_5_out, or_1_out);
  or or_1 (or_1_out, and_1_out, ST_out);
  Demultiplexer #(.select(4), .enable("false")) demultiplexer_1 (
    .out0(demultiplexer_1_out0), .out1(demultiplexer_1_out1), .out2(demultiplexer_1_out2),
    .out3(demultiplexer_1_out3), .out4(demultiplexer_1_out4), .out5(demultiplexer_1_out5),
    .out6(demultiplexer_1_out6), .out7(demultiplexer_1_out7), .out8(demultiplexer_1_out8),
    .out9(demultiplexer_1_out9), .out10(demultiplexer_1_out10), .out11(demultiplexer_1_out11),
    .out12(demultiplexer_1_out12), .out13(demultiplexer_1_out13), .out14(demultiplexer_1_out14),
    .out15(demultiplexer_1_out15), .in(not_5_out), .sel(multiplexer_1_out));
  Multiplexer #(.width(4), .enable("false")) multiplexer_1 (
    .in0(_12_15), .in1(_8_11), .out(multiplexer_1_out), .sel(FN_out));
  Clock clock_1 (.out(clock_1_out));
  Register #(.width(16)) _0 (.D(in_5), .en(demultiplexer_1_out0), .Q(_0_q), .clk(clock_1_out));  // open: clr
  Register #(.width(16)) _1 (.D(in_5), .en(demultiplexer_1_out1), .Q(_1_q), .clk(clock_1_out));  // open: clr
  Register #(.width(16)) _2 (.D(in_5), .en(demultiplexer_1_out2), .Q(_2_q), .clk(clock_1_out));  // open: clr
  Register #(.width(16)) _3 (.D(in_5), .en(demultiplexer_1_out3), .Q(_3_q), .clk(clock_1_out));  // open: clr
  Register #(.width(16)) _4 (.D(in_5), .en(demultiplexer_1_out4), .Q(_4_q), .clk(clock_1_out));  // open: clr
  Register #(.width(16)) _5 (.D(in_5), .en(demultiplexer_1_out5), .Q(_5_q), .clk(clock_1_out));  // open: clr
  Register #(.width(16)) _6 (.D(in_5), .en(demultiplexer_1_out6), .Q(_6_q), .clk(clock_1_out));  // open: clr
  Register #(.width(16)) _7 (.D(in_5), .en(demultiplexer_1_out7), .Q(_7_q), .clk(clock_1_out));  // open: clr
  Register #(.width(16)) _8 (.D(in_5), .en(demultiplexer_1_out8), .Q(_8_q), .clk(clock_1_out));  // open: clr
  Register #(.width(16)) _9 (.D(in_5), .en(demultiplexer_1_out9), .Q(_9_q), .clk(clock_1_out));  // open: clr
  Register #(.width(16)) _10 (.D(in_5), .en(demultiplexer_1_out10), .Q(_10_q), .clk(clock_1_out));  // open: clr
  Register #(.width(16)) _11 (.D(in_5), .en(demultiplexer_1_out11), .Q(_11_q), .clk(clock_1_out));  // open: clr
  Register #(.width(16)) _12 (.D(in_5), .en(demultiplexer_1_out12), .Q(_12_q), .clk(clock_1_out));  // open: clr
  Register #(.width(16)) _13 (.D(in_5), .en(demultiplexer_1_out13), .Q(_13_q), .clk(clock_1_out));  // open: clr
  Register #(.width(16)) _14 (.D(in_5), .en(demultiplexer_1_out14), .Q(_14_q), .clk(clock_1_out));  // open: clr
  Register #(.width(16)) _15 (.D(in_5), .en(demultiplexer_1_out15), .Q(_15_q), .clk(clock_1_out));  // open: clr
  Multiplexer #(.select(4), .width(16), .enable("false")) multiplexer_2 (
    .in0(_0_q), .in1(_1_q), .in2(_2_q), .in3(_3_q), .in4(_4_q), .in5(_5_q), .in6(_6_q), .in7(_7_q),
    .in8(_8_q), .in9(_9_q), .in10(_10_q), .in11(_11_q), .in12(_12_q), .in13(_13_q), .in14(_14_q),
    .in15(_15_q), .out(multiplexer_2_out), .sel(_4_7));
  assign bit_extender_1_out = {{12{1'b0}}, _8_11};  // Bit_Extender bit_extender_1
  Multiplexer #(.select(4), .width(16), .enable("false")) multiplexer_3 (
    .in0(_0_q), .in1(_1_q), .in2(_2_q), .in3(_3_q), .in4(_4_q), .in5(_5_q), .in6(_6_q), .in7(_7_q),
    .in8(_8_q), .in9(_9_q), .in10(_10_q), .in11(_11_q), .in12(_12_q), .in13(_13_q), .in14(_14_q),
    .in15(_15_q), .out(multiplexer_3_out), .sel(_8_11));
  Multiplexer #(.select(4), .width(16), .enable("false")) multiplexer_4 (
    .in0(_0_q), .in1(_1_q), .in2(_2_q), .in3(_3_q), .in4(_4_q), .in5(_5_q), .in6(_6_q), .in7(_7_q),
    .in8(_8_q), .in9(_9_q), .in10(_10_q), .in11(_11_q), .in12(_12_q), .in13(_13_q), .in14(_14_q),
    .in15(_15_q), .sel(_12_15));  // open: out
  Multiplexer #(.width(16), .enable("false")) multiplexer_5 (
    .in0(multiplexer_2_out), .in1(bit_extender_2_out), .out(A), .sel(R_prime_I_out));
  assign bit_extender_2_out = {{12{1'b0}}, _4_7};  // Bit_Extender bit_extender_2
  Multiplexer #(.width(16), .enable("false")) multiplexer_6 (
    .in0(multiplexer_3_out), .in1(bit_extender_1_out), .out(B), .sel(R_prime_I_out));
endmodule

module CU (
  input  [3:0] in_1,
  output out_2,
  output out_3,
  output out_4,
  output out_5,
  output out_6,
  output out_7,
  output out_8
);

  wire bitselector_1_out, bitselector_2_out, bitselector_3_out, bitselector_4_out, not_1_out, not_2_out,
       not_3_out;

  and R_prime_I (out_2, bitselector_1_out, bitselector_2_out, bitselector_3_out);
  BitSelector #(.width(4)) bitselector_1 (.in(in_1), .out(bitselector_1_out), .sel(2'b11));
  and CMP (out_3, bitselector_3_out, bitselector_4_out);
  BitSelector #(.width(4)) bitselector_2 (.in(in_1), .out(bitselector_2_out), .sel(2'b10));
  not not_1 (not_1_out, bitselector_2_out);
  BitSelector #(.width(4)) bitselector_3 (.in(in_1), .out(bitselector_3_out), .sel(2'b01));
  not not_2 (not_2_out, bitselector_3_out);
  and MEM (out_5, bitselector_1_out, bitselector_2_out, not_2_out);
  not not_3 (not_3_out, bitselector_4_out);
  and LD (out_4, out_5, not_3_out);
  BitSelector #(.width(4)) bitselector_4 (.in(in_1), .out(bitselector_4_out), .sel(2'b00));
  and JMP (out_7, bitselector_1_out, not_1_out);
  and ST (out_6, out_5, bitselector_4_out);
  and FN (out_8, out_7, out_3);
endmodule
